// Logisim project tp circuit.circ as structural Verilog: 1 circuit, main circuit main
module main (
  input  X,
  input  Y
);

  wire and_1_out, or_1_out;

  buf and_1 (and_1_out, X);  // AND_Gate
  or or_1 (or_1_out, X, Y);
  _7_Segment_Display u_7_segment_display_1 (
    .f(and_1_out), .a(and_1_out), .b(or_1_out), .e(and_1_out), .d(and_1_out), .c(or_1_out));  // open: g, dp
endmodule
